# Fritzing sketch WateringSystemSketch (saved by Fritzing 0.9.9b)
breadboards: 3

parts:
  Q1 = NPN-BC337 [package="TO92 [THT]"]
  U1 = ESP32S-HiLetgo [part_number=ESP32S-HiLetgo]
  R1 = Resistor [tolerance=±5% power=0.25 resistance=220 package=THT]
  R2 = Resistor [tolerance=±5% power=0.25 resistance=470 package=THT]
  LED1 = DUO LED RG TWO PINS [package="5 mm [THT]"]
  Q2 = NPN-BC337 [package="TO92 [THT]"]
  R3 = Resistor [tolerance=±5% power=0.25 resistance=220 package=THT]
  R4 = Resistor [tolerance=±5% power=0.25 resistance=470 package=THT]
  ZS-042_RTC1 = ZS-042 RTC Module
  U2 = V_REG_7808 [package=78xxl]
  U3 = LM350_Adjustable_Voltage_Regulator [package=78xxl]
  J1 = Power Jack [package=power_jack_pth_lock]
  C1 = 10uF Electrolytic Capacitor [package="100 mil [THT, electrolytic]"]
  C3 = Ceramic Capacitor [capacitance=100nF voltage=35V package="200 mil [THT, multilayer]"]
  D1 = 1N4007 Rectifier Diode [part_number=1N4007 package="300 mil [THT]"]
  D2 = 1N4007 Rectifier Diode [part_number=1N4007 package="300 mil [THT]"]
  C4 = Electrolytic Capacitor [package="200 mil [THT, electrolytic]"]
  C5 = Ceramic Capacitor [capacitance=100nF voltage=35V package="200 mil [THT, multilayer]"]
  C6 = Electrolytic Capacitor [capacitance=100µF voltage=35V package="200 mil [THT, electrolytic]"]
  U4 = 74HC595 [package="DIP16 [THT]"]
  Q3 = NPN-BC337 [package="TO92 [THT]"]
  Q4 = NPN-BC337 [package="TO92 [THT]"]
  U5 = 74HC04_HEX_INVERTER [package=dil14]
  C7 = Ceramic Capacitor [capacitance=100nF voltage=35V package="200 mil [THT, multilayer]"]
  C8 = Ceramic Capacitor [capacitance=100nF voltage=35V package="200 mil [THT, multilayer]"]
  Module1 = AHT20 BMP280 Sensors [package="SO8 [SMD]"]
  microSD1 = MicroSD Card Module
  R5 = Resistor [tolerance=±5% power=0.25 resistance=220 package=THT]
  R6 = Resistor [tolerance=±5% power=0.25 resistance=470 package=THT]
  R7 = Resistor [tolerance=±5% power=0.25 resistance=220 package=THT]
  R8 = Resistor [tolerance=±5% power=0.25 resistance=470 package=THT]
  LED2 = LED - 5mm [color="Red (633nm)" current=0.030 package="5 mm [THT]"]
  LED3 = LED - 5mm [color="Red (633nm)" current=0.030 package="5 mm [THT]"]
  D3 = Diode [package=diode-1n4148]
  C9 = Electrolytic Capacitor [capacitance=1μF voltage=35V package="0405 [SMD, electrolytic]"]
  R9 = Resistor [tolerance=±5% power=0.25 resistance=1M package=THT]
  U6 = 74HC04_HEX_INVERTER [package=dil14]
  C10 = Ceramic Capacitor [capacitance=100nF voltage=35V package="200 mil [THT, multilayer]"]
  J3 = Camdenboss CTB0158-5 [part_number=CTB0158-5 package=THT]
  J4 = Camdenboss CTB0158-5 [part_number=CTB0158-5 package=THT]
  J5 = Camdenboss CTB0158-7 [part_number=CTB0158-7 package=THT]
  D4 = Diode [package=diode-1n4148]
  D5 = Diode [package=diode-1n4148]
  D6 = Diode [package=diode-1n4148]
  D7 = Diode [package=diode-1n4148]
  D8 = Diode [package=diode-1n4148]
  D9 = Diode [package=diode-1n4148]
  D10 = Diode [package=diode-1n4148]
  D11 = Diode [package=diode-1n4148]
  C11 = Ceramic Capacitor [capacitance=100nF voltage=35V package="100 mil [THT, multilayer]"]
  C12 = Ceramic Capacitor [capacitance=100nF voltage=35V package="100 mil [THT, multilayer]"]
  C13 = Ceramic Capacitor [capacitance=100nF voltage=35V package="100 mil [THT, multilayer]"]
  C14 = Ceramic Capacitor [capacitance=100nF voltage=35V package="100 mil [THT, multilayer]"]
  C15 = Ceramic Capacitor [capacitance=100nF voltage=35V package="100 mil [THT, multilayer]"]
  J7 = Camdenboss CTB0158-8 [part_number=CTB0158-8 package=THT]
  C16 = Electrolytic Capacitor [capacitance=100µF voltage=35V package="200 mil [THT, electrolytic]"]
  R10 = Resistor [tolerance=±5% power=0.25 resistance=330 package=THT]
  R11 = Resistor [tolerance=±5% power=0.25 resistance=1.2k package=THT]

nets:
  N1: Q1.C, R1.Pin_1, LED1.red_anode
  N2: Q1.B, R2.Pin_1
  GND: Q1.E, U1.GND, Q2.E, ZS-042_RTC1.GND, U2.GND, J1.GND, C1.-, C3.0, C4.-, C5.1, C6.-, U4.GND, U4.OE, Q3.E, Q4.E, U5.GND, C7.0, C8.0, Module1.GND, microSD1.GND, C9.-, U6.GND, C10.0, J4.pin4, C11.0, C12.0, C13.0, C14.0, C15.0, J7.pin6, C16.-, R11.Pin_0
  VCC: U1.3.3, ZS-042_RTC1.VCC, Module1.VDD
  N3: U1.EN, C1.+
  N4: U1.GPIO36, J5.pin7, C11.1
  N5: U1.GPIO39, D4.C, D5.C, C12.1
  N6: U1.GPIO34, D6.C, D7.C, C13.1
  N7: U1.GPIO35, D8.C, D9.C, C14.1
  N8: U1.GPIO32, D10.C, D11.C, C15.1
  N9: U1.GPIO33, R8.Pin_0
  N10: U1.GPIO25, R6.Pin_0
  N11: U1.GPIO26, R4.Pin_0
  N12: U1.GPIO27, R2.Pin_0
  N13: U1.VIN, U2.OUT, C16.+
  N14: U1.GPIO4, U4.ST_CP
  N15: U1.GPIO16, U4.SH_CP
  N16: U1.GPIO17, U4.DS
  N17: U1.GPIO5, microSD1.CS
  N18: U1.GPIO18, microSD1.SCK
  N19: U1.GPIO19, microSD1.MISO
  N20: U1.GPIO21, ZS-042_RTC1.SDA, Module1.SDA
  N21: U1.GPIO22, ZS-042_RTC1.SCL, Module1.SCL
  N22: U1.GPIO23, microSD1.MOSI
  VCC_2: R1.Pin_0, R3.Pin_0, U3.OUT, D1.anode, D2.cathode, C5.0, C6.+, U4.VCC, U5.VCC, C7.1, C8.1, microSD1.VCC, R5.Pin_0, R7.Pin_0, D3.C, R9.Pin_0, U6.VCC, C10.1, J4.pin5, J7.pin1, R10.Pin_1
  N23: LED1.green_anode, Q2.C, R3.Pin_1
  N24: Q2.B, R4.Pin_1
  N25: U2.IN, U3.IN, J1.PWR, C3.1, D1.cathode, C4.+
  N26: U3.ADJ, D2.anode, R10.Pin_0, R11.Pin_1
  N27: U4.Q1, U5.3A
  N28: U4.Q2, U6.6A
  N29: U4.Q3, U6.5A
  N30: U4.Q4, U6.4A
  N31: U4.Q5, U6.1A
  N32: U4.Q6, U6.2A
  N33: U4.Q7, U6.3A
  N34: U4.MR, D3.A, C9.+, R9.Pin_1
  N35: U4.Q0, U5.2A
  N36: Q3.C, U5.5A, U5.6A, LED2.cathode
  N37: Q3.B, R6.Pin_1
  N38: Q4.C, U5.1A, U5.4A, LED3.cathode
  N39: Q4.B, R8.Pin_1
  N40: U5.1Y, J7.pin2
  N41: U5.2Y, J3.pin1
  N42: U5.3Y, J3.pin2
  N43: U5.4Y, J7.pin3
  N44: U5.5Y, J7.pin4
  N45: U5.6Y, J7.pin5
  N46: R5.Pin_1, LED2.anode
  N47: R7.Pin_1, LED3.anode
  N48: U6.1Y, J4.pin1
  N49: U6.2Y, J4.pin2
  N50: U6.3Y, J4.pin3
  N51: U6.4Y, J3.pin5
  N52: U6.5Y, J3.pin4
  N53: U6.6Y, J3.pin3
  N54: J5.pin1, D9.A
  N55: J5.pin2, D8.A
  N56: J5.pin3, D7.A
  N57: J5.pin4, D6.A
  N58: J5.pin5, D4.A
  N59: J5.pin6, D5.A
  N60: D10.A, J7.pin8
  N61: D11.A, J7.pin7

notes:
  +12V DC Input
  12V - yellow wire
  8V - pink wire
  5V - red wire
  3.3V - orange wire
  GND - black wire
  74HC595
  Reset
  Circut
  R9, D3, C9
  74HC595
  Reset
  Circut
  Power ON CHANNEL 1
  Power ON CHANNEL 2
  Power Sensors
  on CHANNEL 1
  Power Sensors
  on CHANNEL 2
  Watering Valves Controll Outputs
  Valve 1
  Valve 2
  Valve 3
  Valve 4
  Valve 5
  Valve 6
  Valve 7
  Valve 8
  GND
  Vcc +5V
  Status LED
  Wetness and Rain sensors Input
  +5V, Power ON CH2, CH1, GND,
  Wetnes 8-1, Rain
  Wetness and Rain sensors Input
  +5V
  Power ON CH2, CH1, GND, Wetnes 8-1, Rain

custom parts:
  NPN-BC337: A standard NPN-transistor
  ESP32S-HiLetgo: HiLetgo ESP-WROOM-32 ESP32 ESP-32S Development Board 2.4GHz Dual-Mode WiFi + Bluetooth Dual Cores Microcontroller The ESP32 integrated with Antenna switches, RF Balun, power amplifiers, low-noise amplifiers, filters, and management modules, and the entire solution occupies the least area of PCB. 2.4 GHz Wi-Fi plus Bluetooth dual-mode chip, with TSMC Ultra-low power consumption 40nm technology,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
  DUO LED RG TWO PINS: A 5mm DUO-color LED with red and green inside.
  V_REG_7808: LM7808 voltage regulator
  LM350_Adjustable_Voltage_Regulator: LM350 Adjustable Voltage Regulator
  10uF Electrolytic Capacitor: A small electrolytic capacitor
  1N4007 Rectifier Diode: A standard rectifier diode
  Electrolytic Capacitor: electrolytic capacitor
  AHT20 BMP280 Sensors: AHT20+BMP280 Temperature humidity Air Pressure Sensor Module High-Precision
